# Fritzing sketch EMETTEUR + CABLAGE DES COMPOSANTS (saved by Fritzing 0.9.3b)
stripboards: 1
breadboards: 1

parts:
  Composant1 = Arduino Uno (Rev3)
  DHT1 = DHT22 Humidity and Temperature Sensor
  Composant2 = Adafruit Ultimate GPS v3 [part_number="Adafruit #746"]
  Composant3 = 10-DOF IMU L3GD20H + LSM303 + BMP180 [part_number=1604]
  Composant4 = GUVA-S12SD UV Light Sensor
  Composant5 = Adafruit RFM69HCW Transceiver Radio [part_number="Adafruit #3070 and #3071"]
  Composant6 = Ambient Light Sensor (TEMT6000 Breakout Board)
  R1 = Resistor [tolerance=±5% resistance=220 package="2010 [SMD]"]

nets:
  N1: Composant1.A1, Composant4.Out
  N2: Composant1.A2, Composant6.S
  N3: Composant1.A4/SDA, Composant3.SDA
  N4: Composant1.A5/SCL, Composant3.SCL
  N5: Composant1.D9_PWM, Composant5.RST
  N6: Composant1.D10_PWM/SS, Composant5.CS
  N7: Composant1.D11_PWM/MOSI, Composant5.MOSI
  N8: Composant1.D12/MISO, Composant5.MISO
  N9: Composant1.D13/SCK, Composant5.SCK
  N10: Composant1.D2, Composant5.DIO0
  N11: Composant1.D3_PWM, Composant2.TX
  N12: Composant1.D4, Composant2.RX
  N13: Composant1.D6_PWM, DHT1.DATA, R1.Pin_1
  VIN: Composant1.5V, DHT1.VDD, Composant2.VIN, Composant3.VIN, Composant4.5V, Composant5.VIN, Composant6.VCC, R1.Pin_0
  GND: Composant1.GND, DHT1.GND, Composant2.GND, Composant3.GND, Composant4.GND, Composant5.GND, Composant6.GND

notes:
  Antenne: 16.5 cm

custom parts:
  Adafruit Ultimate GPS v3: We carry a few different GPS modules here in the Adafruit shop, but none that satisfied our every desire - that's why we designed this little GPS breakout board. We believe this is the Ultimate GPS module, so we named it that. It's got everything you want and more: -165 dBm sensitivity, 10 Hz updates, 66 channels 5V friendly design and only 20mA current draw Breadboard friendly + two mounting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
  10-DOF IMU L3GD20H + LSM303 + BMP180: This inertial-measurement-unit combines 3 of the best quality sensors available on the market to give you 11 axes of data: 3 axes of accelerometer data, 3 axes gyroscopic, 3 axes magnetic (compass), barometric pressure/altitude and temperature. We tested many different 'combination' sensors and found these were the best value, with stable and reliable readings.
  GUVA-S12SD UV Light Sensor: Extend your light-sensing spectrum with this analog UV sensor module. It uses a UV photodiode, which can detect the 240-370nm range of light (which covers UVB and most of UVA spectrum). The signal level from the photodiode is very small, in the nano-ampere level, so we tossed on an opamp to amplify the signal to a more manageable volt-level.
  Adafruit RFM69HCW Transceiver Radio: Sending data over long distances is like magic, and now you can be a magician with this range of powerful and easy-to-use radio modules. Sure, sometimes you want to talk to a computer (a good time to use WiFi) or perhaps communicate with a Phone (choose Bluetooth Low Energy!) but what if you want to send data very far? Most WiFi, Bluetooth, Zigbee and other wireless chipsets use 2.4GHz, which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
