# Fritzing sketch RECEPTEUR (ARDUINO MEGA)  + RFM69HCW  (saved by Fritzing 0.9.3b)

parts:
  Composant5 = Adafruit RFM69HCW Transceiver Radio [part_number="Adafruit #3070 and #3071"]
  Composant6 = Arduino Mega 2560 (Rev3)

nets:
  VIN: Composant5.VIN, Composant6.5V
  GND: Composant5.GND, Composant6.GND
  N1: Composant5.DIO0, Composant6.D2_PWM
  N2: Composant5.SCK, Composant6.D52
  N3: Composant5.MISO, Composant6.D50
  N4: Composant5.MOSI, Composant6.D51
  N5: Composant5.CS, Composant6.D10_PWM
  N6: Composant5.RST, Composant6.D9_PWM

notes:
  Antenne: 16.5 cm

custom parts:
  Adafruit RFM69HCW Transceiver Radio: Sending data over long distances is like magic, and now you can be a magician with this range of powerful and easy-to-use radio modules. Sure, sometimes you want to talk to a computer (a good time to use WiFi) or perhaps communicate with a Phone (choose Bluetooth Low Energy!) but what if you want to send data very far? Most WiFi, Bluetooth, Zigbee and other wireless chipsets use 2.4GHz, which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
